# Fritzing sketch Schematic (saved by Fritzing 1.0.2b)
breadboards: 1

parts:
  Mod1 = Raspberry Pi Pico W
  LED1 = LED - 5mm [color="Blue (470nm)" current=0.030A package="5 mm [THT]"]
  R1 = Resistor [tolerance=±1% power=0.25W resistance=220 package=THT]
  Motion_Sensor = InvenSense MPU6050

nets:
  N1: Mod1.pin_3, Mod1.pin_8, Mod1.pin_13, Mod1.pin_18, Mod1.pin_23, Mod1.pin_28, Mod1.pin_33, Mod1.pin_38, Mod1.pin_42, R1.Pin_1, Motion_Sensor.GND
  N2: Mod1.pin_6, Motion_Sensor.SDA
  N3: Mod1.pin_7, Motion_Sensor.SCL
  N4: Mod1.pin_21, LED1.anode
  N5: Mod1.pin_40, Motion_Sensor.VCC
  N6: LED1.cathode, R1.Pin_0

custom parts:
  Raspberry Pi Pico W: Raspberry Pi Pico W. Based around the RP2040 microcontroller the Pico W is a low cost microcontroller device bringing Raspberry Pi quality, cost, and easy of use to the microcontroller space. The areas marked KEEPOUT in pcb silkscreen should not have traces running through them to avoid shorts on a soldered in module!
